// Logisim project 1 Bit ALU.circ as structural Verilog: 1 circuit, main circuit main
module main (
  input  Cin,
  input  A,
  input  B,
  input  [2:0] Op_Code,
  input  B_Inv,
  input  Less,
  output Result,
  output Cout,
  output Set
);

  wire and_1_out, multiplexer_1_out, multiplexer_2_out, nor_1_out, not_1_out, or_1_out;

  not not_1 (not_1_out, B);
  Multiplexer #(.enable("false")) multiplexer_1 (.in0(B), .in1(not_1_out), .out(multiplexer_1_out), .sel(B_Inv));
  Multiplexer #(.enable("false")) multiplexer_2 (.in0(1'b0), .in1(1'b1), .out(multiplexer_2_out), .sel(Less));
  and and_1 (and_1_out, B, A);
  or or_1 (or_1_out, B, A);
  nor nor_1 (nor_1_out, B, A);
  Adder #(.width(1)) adder_1 (.a(multiplexer_1_out), .b(A), .out(Set), .cin(Cin), .cout(Cout));
  Multiplexer #(.select(3), .enable("false")) multiplexer_3 (
    .in0(and_1_out), .in1(or_1_out), .in2(nor_1_out), .in3(Set), .in4(multiplexer_2_out), .in5(Set),
    .out(Result), .sel(Op_Code));  // open: in6, in7

  // Notes on the sheet:
  //   010
  //   000
  //   001
  //   100
  //   011
  //   101
endmodule
