// Logisim project 12 Bit Processor.circ as structural Verilog: 1 circuit, main circuit main
module main (
  input  in_1,
  input  [11:0] A,
  input  [11:0] B,
  input  [2:0] OpCode,
  input  B_Invert,
  input  Result_sll,
  output [11:0] Result,
  output Zero,
  output Cout,
  output Overflow
);

  wire main_1_cout, main_2_cout, main_3_cout, main_4_cout, main_5_cout, main_6_cout, main_7_cout,
       main_8_cout, main_9_cout, main_10_cout, main_11_cout, main_12_set;
  wire [3:0] bit_extender_1_out;
  wire [11:0] main_1_result, shifter_1_out;

  _1_Bit_ALU_main main_1 (
    .Cin(in_1), .Result(main_1_result[0]), .A(A[0]), .B(B[0]), .Cout(main_1_cout), .Op_Code(OpCode),
    .Less(main_12_set), .B_Inv(B_Invert));  // open: Set
  Multiplexer #(.width(12), .enable("false")) multiplexer_1 (
    .in0(main_1_result), .in1(shifter_1_out), .out(Result), .sel(Result_sll));
  _1_Bit_ALU_main main_2 (
    .Cin(main_1_cout), .Result(main_1_result[1]), .A(A[1]), .B(B[1]), .Cout(main_2_cout), .Op_Code(OpCode),
    .Less(1'b0), .B_Inv(B_Invert));  // open: Set
  _1_Bit_ALU_main main_3 (
    .Cin(main_2_cout), .Result(main_1_result[2]), .A(A[2]), .B(B[2]), .Cout(main_3_cout), .Op_Code(OpCode),
    .Less(1'b0), .B_Inv(B_Invert));  // open: Set
  _1_Bit_ALU_main main_4 (
    .Cin(main_3_cout), .Result(main_1_result[3]), .A(A[3]), .B(B[3]), .Cout(main_4_cout), .Op_Code(OpCode),
    .Less(1'b0), .B_Inv(B_Invert));  // open: Set
  _1_Bit_ALU_main main_5 (
    .Cin(main_4_cout), .Result(main_1_result[4]), .A(A[4]), .B(B[4]), .Cout(main_5_cout), .Op_Code(OpCode),
    .Less(1'b0), .B_Inv(B_Invert));  // open: Set
  _1_Bit_ALU_main main_6 (
    .Cin(main_5_cout), .Result(main_1_result[5]), .A(A[5]), .B(B[5]), .Cout(main_6_cout), .Op_Code(OpCode),
    .Less(1'b0), .B_Inv(B_Invert));  // open: Set
  or or_1 (Zero, main_1_result[0], main_1_result[1], main_1_result[2], main_1_result[3], main_1_result[4], main_1_result[5], main_1_result[6], main_1_result[7], main_1_result[8], main_1_result[9], main_1_result[10], main_1_result[11]);
  _1_Bit_ALU_main main_7 (
    .Cin(main_6_cout), .Result(main_1_result[6]), .A(A[6]), .B(B[6]), .Cout(main_7_cout), .Op_Code(OpCode),
    .Less(1'b0), .B_Inv(B_Invert));  // open: Set
  _1_Bit_ALU_main main_8 (
    .Cin(main_7_cout), .Result(main_1_result[7]), .A(A[7]), .B(B[7]), .Cout(main_8_cout), .Op_Code(OpCode),
    .Less(1'b0), .B_Inv(B_Invert));  // open: Set
  Bit_Extender #(.in_width(12), .out_width(4)) bit_extender_1 (.in(B), .out(bit_extender_1_out));
  xor xor_1 (Overflow, main_11_cout, Cout);
  Shifter #(.width(12)) shifter_1 (.in(A), .\dist (bit_extender_1_out), .out(shifter_1_out));
  _1_Bit_ALU_main main_9 (
    .Cin(main_8_cout), .Result(main_1_result[8]), .A(A[8]), .B(B[8]), .Cout(main_9_cout), .Op_Code(OpCode),
    .Less(1'b0), .B_Inv(B_Invert));  // open: Set
  _1_Bit_ALU_main main_10 (
    .Cin(main_9_cout), .Result(main_1_result[9]), .A(A[9]), .B(B[9]), .Cout(main_10_cout), .Op_Code(OpCode),
    .Less(1'b0), .B_Inv(B_Invert));  // open: Set
  _1_Bit_ALU_main main_11 (
    .Cin(main_10_cout), .Result(main_1_result[10]), .A(A[10]), .B(B[10]), .Cout(main_11_cout),
    .Op_Code(OpCode), .Less(1'b0), .B_Inv(B_Invert));  // open: Set
  _1_Bit_ALU_main main_12 (
    .Cin(main_11_cout), .Result(main_1_result[11]), .A(A[11]), .B(B[11]), .Cout(Cout), .Op_Code(OpCode),
    .Set(main_12_set), .Less(1'b0), .B_Inv(B_Invert));
endmodule
