// Logisim project Datapath V2.circ as structural Verilog: 1 circuit, main circuit main
module main (
  output [11:0] Result,
  output Cout,
  output Zero,
  output Overflow,
  output [11:0] out_5
);

  wire _0_out, _1_out, _2_out, _3_out, _4_out, _5_out, _6_out, _7_out, and_1_out, CLK_out, E_out,
       main_1_binv, main_1_bne, main_1_cin, main_1_format, main_1_in, main_1_jump, main_1_out,
       main_1_resultload, main_1_resultsll, main_1_store, minus_1_out, minus_2_out, minus_3_out, minus_4_out,
       minus_5_out, minus_6_out, minus_7_out, multiplexer_1_out;
  wire [2:0] main_1_al2;
  wire [3:0] demultiplexer_1_out0, demultiplexer_1_out1, input_circuit_1_out_17, rom_1_data_2;
  wire [7:0] rom_1_data;
  wire [11:0] adder_1_out, bit_extender_1_out, main_2_a, main_2_b, main_2_spr, multiplexer_2_out,
       multiplexer_3_out, multiplexer_4_out, multiplexer_5_out, multiplexer_6_out, multiplexer_7_out,
       ram_1_data, register_1_q, register_2_q;

  Clock CLK (.out(CLK_out));
  Multiplexer #(.enable("false")) multiplexer_1 (.in0(CLK_out), .in1(E_out), .out(multiplexer_1_out), .sel(main_1_in));
  Register #(.width(12)) register_1 (.D(adder_1_out), .Q(register_1_q), .clk(multiplexer_1_out));  // open: en, clr
  Adder #(.width(12)) adder_1 (.a(register_1_q), .b(multiplexer_4_out), .out(adder_1_out));  // open: cin, cout
  and and_1 (and_1_out, Zero, main_1_bne);
  ROM #(.addrWidth(12), .dataWidth(12)) rom_1 (.addr(register_1_q), .data({rom_1_data_2, rom_1_data}));  // open: sel
  Multiplexer #(.width(12), .enable("false")) multiplexer_2 (
    .in0(12'h1), .in1(bit_extender_1_out), .out(multiplexer_2_out), .sel(and_1_out));
  Multiplexer #(.width(12), .enable("false")) multiplexer_3 (
    .in0(multiplexer_6_out), .in1(out_5), .out(multiplexer_3_out), .sel(main_1_in));
  Demultiplexer #(.width(4), .enable("false")) demultiplexer_1 (
    .out0(demultiplexer_1_out0), .out1(demultiplexer_1_out1), .in(rom_1_data[3:0]), .sel(main_1_format));
  Multiplexer #(.width(12), .enable("false")) multiplexer_4 (
    .in0(multiplexer_2_out), .in1(bit_extender_1_out), .out(multiplexer_4_out), .sel(main_1_jump));
  Control_Unit_main main_1 (
    .A(rom_1_data_2[3]), .B(rom_1_data_2[2]), .C(rom_1_data_2[1]), .Format(main_1_format),
    .D(rom_1_data_2[0]), .AL0(main_1_al2[2]), .AL1(main_1_al2[1]), .AL2(main_1_al2[0]), .In(main_1_in),
    .ResultLoad(main_1_resultload), .Store(main_1_store), .ResultSll(main_1_resultsll), .Cin(main_1_cin),
    .Binv(main_1_binv), .bne(main_1_bne), .jump(main_1_jump), .Out(main_1_out));
  assign bit_extender_1_out = {{8{demultiplexer_1_out1[3]}}, demultiplexer_1_out1};  // Bit_Extender bit_extender_1
  Hex_Digit_Display hex_digit_display_1 (.value(register_2_q[11:8]));  // open: dp
  Hex_Digit_Display hex_digit_display_2 (.value(register_2_q[3:0]));  // open: dp
  Hex_Digit_Display hex_digit_display_3 (.value(register_2_q[7:4]));  // open: dp
  Multiplexer #(.width(12), .enable("false")) multiplexer_5 (
    .in0(main_2_b), .in1(bit_extender_1_out), .out(multiplexer_5_out), .sel(main_1_format));
  Register #(.width(12)) register_2 (
    .D(main_2_a), .en(main_1_out), .Q(register_2_q), .clk(multiplexer_1_out));  // open: clr
  Register_File_Design_main main_2 (
    .set_value_in_reg(multiplexer_3_out), .reg__selector(rom_1_data[7:4]), .A(main_2_a), .B(main_2_b),
    .rd(rom_1_data[7:4]), .rs(demultiplexer_1_out0), .in_5(multiplexer_1_out), .spr(main_2_spr));
  Multiplexer #(.width(12), .enable("false")) multiplexer_6 (
    .in0(Result), .in1(ram_1_data), .out(multiplexer_6_out), .sel(main_1_resultload));
  _12_Bit_Processor_main main_3 (
    .Overflow(Overflow), .in_1(main_1_cin), .OpCode(main_1_al2), .Result(Result), .A(main_2_a),
    .B(multiplexer_7_out), .Zero(Zero), .Cout(Cout), .B_Invert(main_1_binv), .Result_sll(main_1_resultsll));
  Multiplexer #(.width(12), .enable("false")) multiplexer_7 (
    .in0(multiplexer_5_out), .in1(main_2_spr), .out(multiplexer_7_out), .sel(main_1_bne));
  RAM #(.addrWidth(12), .dataWidth(12), .bus("separate")) ram_1 (
    .addr(main_2_b), .din(main_2_a), .data(ram_1_data), .str(main_1_store), .clk(multiplexer_1_out),
    .ld(main_1_resultload));  // open: sel, clr
  Button _0 (.out(_0_out));
  Button _4 (.out(_4_out));
  Button minus_7 (.out(minus_7_out));
  Button _2 (.out(_2_out));
  Button _1 (.out(_1_out));
  Button _5 (.out(_5_out));
  Button _6 (.out(_6_out));
  Button minus_5 (.out(minus_5_out));
  Button minus_6 (.out(minus_6_out));
  Button minus_3 (.out(minus_3_out));
  Button minus_2 (.out(minus_2_out));
  Button E (.out(E_out));
  Button _3 (.out(_3_out));
  Button _7 (.out(_7_out));
  Button minus_4 (.out(minus_4_out));
  Button minus_1 (.out(minus_1_out));
  assign out_5 = {{8{input_circuit_1_out_17[3]}}, input_circuit_1_out_17};  // Bit_Extender bit_extender_2
  Input_Circuit input_circuit_1 (
    ._0(_0_out), ._1(_1_out), ._2(_2_out), ._3(_3_out), ._4(_4_out), ._5(_5_out), ._6(_6_out), ._7(_7_out),
    .minus_7(minus_7_out), .minus_6(minus_6_out), .minus_5(minus_5_out), .minus_4(minus_4_out),
    .minus_3(minus_3_out), .minus_2(minus_2_out), .minus_1(minus_1_out), .out_17(input_circuit_1_out_17));  // open: in_1

  // Other names for the same wires on the sheet: A[11:0] = out_5

  // Notes on the sheet:
  //   contents of rom_1 (hex, n*v repeats v):
  //   5a2 554 9f0 8a5 522 542 64 796 a90 e9a
endmodule
