// Logisim project Input.circ as structural Verilog: 3 circuits, main circuit Input Circuit
module Decimal_to_BCD (
  input  _0,
  input  _1,
  input  _2,
  input  _3,
  input  _4,
  input  _5,
  input  _6,
  input  _7,
  input  x,
  input  minus_7,
  input  minus_6,
  input  minus_5,
  input  minus_4,
  input  minus_3,
  input  minus_2,
  input  minus_1,
  output A,
  output B,
  output C,
  output D
);

  or or_1 (A, x, minus_7, minus_6, minus_5, minus_4, minus_3, minus_2, minus_1);
  or or_2 (B, _4, _5, _6, _7, minus_4, minus_3, minus_2, minus_1);
  or or_3 (C, _2, _3, _7, _6, minus_6, minus_5, minus_2, minus_1);
  or or_4 (D, _1, _3, minus_1, _5, _7, minus_3, minus_7, minus_5);
endmodule

module Input_Circuit (
  input  in_1,
  input  _0,
  input  _1,
  input  _2,
  input  _3,
  input  _4,
  input  _5,
  input  _6,
  input  _7,
  input  minus_7,
  input  minus_6,
  input  minus_5,
  input  minus_4,
  input  minus_3,
  input  minus_2,
  input  minus_1,
  output [3:0] out_17
);

  wire decimal_to_bcd_1_a, decimal_to_bcd_1_b, decimal_to_bcd_1_c, decimal_to_bcd_1_d;

  Decimal_to_BCD decimal_to_bcd_1 (
    ._0(_0), ._1(_1), ._2(_2), ._3(_3), ._4(_4), ._5(_5), ._6(_6), ._7(_7), .x(1'b0), .minus_7(minus_7),
    .minus_6(minus_6), .minus_5(minus_5), .minus_4(minus_4), .minus_3(minus_3), .minus_2(minus_2),
    .minus_1(minus_1), .A(decimal_to_bcd_1_a), .B(decimal_to_bcd_1_b), .C(decimal_to_bcd_1_c),
    .D(decimal_to_bcd_1_d));
  Input_Memory input_memory_1 (
    .in_1(decimal_to_bcd_1_d), .in_2(decimal_to_bcd_1_c), .in_3(decimal_to_bcd_1_b),
    .in_4(decimal_to_bcd_1_a), .in_5(_0), .out_6(out_17));

  assign in_1 = _0;
endmodule

module Input_Memory (
  input  in_1,
  input  in_2,
  input  in_3,
  input  in_4,
  input  in_5,
  output [3:0] out_6
);

  wire or_1_out;

  or or_1 (or_1_out, in_1, in_2, in_3, in_4);
  Register #(.width(4)) register_1 (.D({in_4, in_3, in_2, in_1}), .Q(out_6), .clk(or_1_out), .clr(in_5));  // open: en
endmodule
