// Logisim project Register File Design.circ as structural Verilog: 1 circuit, main circuit main
module main (
  input  [11:0] set_value_in_reg,
  input  [3:0] reg__selector,
  input  [3:0] rd,
  input  [3:0] rs,
  input  in_5,
  output [11:0] spr,
  output [11:0] A,
  output [11:0] B
);

  wire decoder_1_out0, decoder_1_out1, decoder_1_out2, decoder_1_out3, decoder_1_out4, decoder_1_out5,
       decoder_1_out6, decoder_1_out7, decoder_1_out8, decoder_1_out9, decoder_1_out10, decoder_1_out11,
       decoder_1_out12, decoder_1_out13, decoder_1_out14, decoder_1_out15;
  wire [11:0] register_1_q, register_3_q, register_4_q, register_5_q, register_6_q, register_7_q,
       register_8_q, register_9_q, register_10_q, register_11_q, register_12_q, register_13_q, register_14_q,
       register_15_q, register_16_q;

  Decoder #(.select(4), .enable("false")) decoder_1 (
    .out0(decoder_1_out0), .out1(decoder_1_out1), .out2(decoder_1_out2), .out3(decoder_1_out3),
    .out4(decoder_1_out4), .out5(decoder_1_out5), .out6(decoder_1_out6), .out7(decoder_1_out7),
    .out8(decoder_1_out8), .out9(decoder_1_out9), .out10(decoder_1_out10), .out11(decoder_1_out11),
    .out12(decoder_1_out12), .out13(decoder_1_out13), .out14(decoder_1_out14), .out15(decoder_1_out15),
    .sel(reg__selector));
  Register #(.width(12)) register_1 (.D({12{1'b0}}), .en(decoder_1_out0), .Q(register_1_q), .clk(in_5));  // open: clr
  Register #(.width(12)) register_2 (.D(set_value_in_reg), .en(decoder_1_out1), .Q(spr), .clk(in_5));  // open: clr
  Register #(.width(12)) register_3 (
    .D(set_value_in_reg), .en(decoder_1_out2), .Q(register_3_q), .clk(in_5));  // open: clr
  Register #(.width(12)) register_4 (
    .D(set_value_in_reg), .en(decoder_1_out3), .Q(register_4_q), .clk(in_5));  // open: clr
  Register #(.width(12)) register_5 (
    .D(set_value_in_reg), .en(decoder_1_out4), .Q(register_5_q), .clk(in_5));  // open: clr
  Register #(.width(12)) register_6 (
    .D(set_value_in_reg), .en(decoder_1_out5), .Q(register_6_q), .clk(in_5));  // open: clr
  Register #(.width(12)) register_7 (
    .D(set_value_in_reg), .en(decoder_1_out6), .Q(register_7_q), .clk(in_5));  // open: clr
  Register #(.width(12)) register_8 (
    .D(set_value_in_reg), .en(decoder_1_out7), .Q(register_8_q), .clk(in_5));  // open: clr
  Register #(.width(12)) register_9 (
    .D(set_value_in_reg), .en(decoder_1_out8), .Q(register_9_q), .clk(in_5));  // open: clr
  Register #(.width(12)) register_10 (
    .D(set_value_in_reg), .en(decoder_1_out9), .Q(register_10_q), .clk(in_5));  // open: clr
  Register #(.width(12)) register_11 (
    .D(set_value_in_reg), .en(decoder_1_out10), .Q(register_11_q), .clk(in_5));  // open: clr
  Register #(.width(12)) register_12 (
    .D(set_value_in_reg), .en(decoder_1_out11), .Q(register_12_q), .clk(in_5));  // open: clr
  Register #(.width(12)) register_13 (
    .D(set_value_in_reg), .en(decoder_1_out12), .Q(register_13_q), .clk(in_5));  // open: clr
  Register #(.width(12)) register_14 (
    .D(set_value_in_reg), .en(decoder_1_out13), .Q(register_14_q), .clk(in_5));  // open: clr
  Register #(.width(12)) register_15 (
    .D(set_value_in_reg), .en(decoder_1_out14), .Q(register_15_q), .clk(in_5));  // open: clr
  Register #(.width(12)) register_16 (
    .D(set_value_in_reg), .en(decoder_1_out15), .Q(register_16_q), .clk(in_5));  // open: clr
  Multiplexer #(.select(4), .width(12), .enable("false")) multiplexer_1 (
    .in0(register_1_q), .in1(spr), .in2(register_3_q), .in3(register_4_q), .in4(register_5_q),
    .in5(register_6_q), .in6(register_7_q), .in7(register_8_q), .in8(register_9_q), .in9(register_10_q),
    .in10(register_11_q), .in11(register_12_q), .in12(register_13_q), .in13(register_14_q),
    .in14(register_15_q), .in15(register_16_q), .out(A), .sel(rd));
  Multiplexer #(.select(4), .width(12), .enable("false")) multiplexer_2 (
    .in0(register_1_q), .in1(spr), .in2(register_3_q), .in3(register_4_q), .in4(register_5_q),
    .in5(register_6_q), .in6(register_7_q), .in7(register_8_q), .in8(register_9_q), .in9(register_10_q),
    .in10(register_11_q), .in11(register_12_q), .in12(register_13_q), .in13(register_14_q),
    .in14(register_15_q), .in15(register_16_q), .out(B), .sel(rs));

  // Notes on the sheet:
  //   $s1
  //   $s2
  //   $s3
  //   $s5
  //   $s6
  //   $s7
  //   $t0
  //   $t1
  //   $t2
  //   $t3
  //   $zero
  //   $spr
  //   $s4
  //   $t4
  //   $t5
  //   $t6
  //   Register File
endmodule
